# Fritzing sketch Wiring_diag (saved by Fritzing 1.0.4)
breadboards: 1

parts:
  M1 = fc-51 [package=THT]
  M2 = fc-51 [package=THT]
  LED1 = smd LED [color="Red (633nm)" package="0805 [SMD]"]
  LED2 = smd LED [color="Red (633nm)" package="0805 [SMD]"]
  Part1 = Arduino Mega 2560 (Rev3)
  HC-SR04_Sensor_1 = HC-SR04 Ultrasonic Distance Sensor
  Part2 = NRF24L01+ Breakout Board
  J1 = Piezo Speaker
  Part3 = Humidity Sensor - HIH-4030 Breakout
  Part4 = Humidity Sensor - HIH-4030 Breakout
  J2 = Basic Servo
  R1 = Resistor [tolerance=±5% power=0.25W resistance=220 package=THT]
  R2 = Resistor [tolerance=±5% power=0.25W resistance=220 package=THT]

nets:
  N1: M1.pin1, Part1.D34
  GND: M1.pin2, M2.pin2, Part1.GND, HC-SR04_Sensor_1.GND, Part2.GND, J1.pin1, Part3.GND, Part4.GND, R1.Pin_0, R2.Pin_0
  VCC: M1.pin3, M2.pin3, Part1.5V, HC-SR04_Sensor_1.VCC, Part3.VCC, Part4.VCC, J2.vcc
  N2: M2.pin1, Part1.D35
  N3: LED1.cathode, R2.Pin_1
  N4: LED1.anode, Part1.D36
  N5: LED2.cathode, R1.Pin_1
  N6: LED2.anode, Part1.D37
  N7: Part1.A2, Part3.OUT
  N8: Part1.A3, Part4.OUT
  N9: Part1.D13_PWM, J2.pulse
  3V3: Part1.3V3, Part2.VCC
  N10: Part1.D42, HC-SR04_Sensor_1.ECHO
  N11: Part1.D43, HC-SR04_Sensor_1.TRIG
  N12: Part1.D48, Part2.CE
  N13: Part1.D49, Part2.CS
  N14: Part1.D50, Part2.MISO
  N15: Part1.D51, Part2.MOSI
  N16: Part1.D52, Part2.SCK

notes:
  For Ladder
  QTI Sensors
